# Fritzing sketch client (saved by Fritzing 0.9.3b)
breadboards: 1

parts:
  Bauteil1 = Arduino Uno (Rev3)
  LED1 = LED - 5mm [color="Red (633nm)" package="5 mm [THT]"]
  LED2 = LED - 5mm [color="Yellow (592nm)" package="5 mm [THT]"]
  LED3 = LED - 5mm [color="Green (565nm)" package="5 mm [THT]"]
  R1 = Resistor [tolerance=±5% resistance=220 package=THT]

nets:
  N1: Bauteil1.D8, LED1.anode
  N2: Bauteil1.D10_PWM/SS, LED2.anode
  N3: Bauteil1.D12/MISO, LED3.anode
  N4: Bauteil1.GND, R1.Pin_1
  N5: LED1.cathode, LED2.cathode, LED3.cathode, R1.Pin_0

notes:
  Add USB-cable for power here!
