# Fritzing sketch server (saved by Fritzing 0.9.3b)

parts:
  Raspberry_Pi_1 = Raspberry Pi 3 [part_number=RPI-3-V1.2]
  Bauteil1 = Arduino Uno (Rev3)

nets:
  N1: Raspberry_Pi_1.GPIO2, Bauteil1.A4/SDA
  N2: Raspberry_Pi_1.GPIO3, Bauteil1.A5/SCL
  GND: Raspberry_Pi_1.GND, Bauteil1.GND
